# Fritzing sketch Clock Display (saved by Fritzing 0.9.3b)
breadboards: 3

parts:
  U1 = 74HC595 [package="DIP16 [THT]"]
  R1 = Resistor [tolerance=±5% resistance=270 package="0402 [SMD]"]
  R2 = Resistor [tolerance=±5% resistance=270 package="0402 [SMD]"]
  R3 = Resistor [tolerance=±5% resistance=270 package="0402 [SMD]"]
  R4 = Resistor [tolerance=±5% resistance=270 package="0402 [SMD]"]
  R5 = Resistor [tolerance=±5% resistance=270 package="0402 [SMD]"]
  R6 = Resistor [tolerance=±5% resistance=270 package="0402 [SMD]"]
  R7 = Resistor [tolerance=±5% resistance=270 package="0402 [SMD]"]
  R8 = Resistor [tolerance=±5% resistance=220 package="0402 [SMD]"]
  LED3 = 7-SEGMENT-4DIGIT-ATA8041AB [part_number=ATA8041AB package=7-segment-4digit-youngsun-longpads]
  Part1 = Arduino Pro Mini (5V)
  U2 = 74HC595 [package="DIP16 [THT]"]
  R9 = Resistor [tolerance=±5% resistance=220 package="0402 [SMD]"]
  R10 = Resistor [tolerance=±5% resistance=270 package="0402 [SMD]"]
  R11 = Resistor [tolerance=±5% resistance=270 package="0402 [SMD]"]
  R12 = Resistor [tolerance=±5% resistance=270 package="0402 [SMD]"]
  R13 = Resistor [tolerance=±5% resistance=270 package="0402 [SMD]"]
  R14 = Resistor [tolerance=±5% resistance=270 package="0402 [SMD]"]
  R15 = Resistor [tolerance=±5% resistance=270 package="0402 [SMD]"]
  R16 = Resistor [tolerance=±5% resistance=270 package="0402 [SMD]"]
  LED4 = 7-SEGMENT-4DIGIT-ATA8041AB [part_number=ATA8041AB package=7-segment-4digit-youngsun-longpads]

nets:
  N1: U1.Q1, R7.Pin_1
  N2: U1.Q2, R4.Pin_1
  N3: U1.Q3, R5.Pin_1
  N4: U1.Q4, R3.Pin_1
  N5: U1.Q5, R2.Pin_1
  N6: U1.Q6, R1.Pin_1
  N7: U1.Q7, R8.Pin_1
  N8: U1.GND, U1.OE
  N9: U1.Q7', U2.DS
  VCC: U1.MR, U1.VCC, Part1.VCC
  N10: U1.SH_CP, U2.SH_CP
  N11: U1.ST_CP, U2.ST_CP
  N12: U1.Q0, R6.Pin_1
  N13: R1.Pin_0, LED3.10
  N14: R2.Pin_0, LED3.5
  N15: R3.Pin_0, LED3.4
  N16: R4.Pin_0, LED3.2
  N17: R5.Pin_0, LED3.3
  N18: R6.Pin_0, LED3.11
  N19: R7.Pin_0, LED3.1
  N20: R8.Pin_0, LED3.7
  N21: LED3.6, LED4.6
  N22: LED3.8, LED4.8
  N23: LED3.9, LED4.9
  N24: LED3.12, LED4.12
  N25: U2.Q1, R10.Pin_1
  N26: U2.Q2, R13.Pin_1
  N27: U2.Q3, R12.Pin_1
  N28: U2.Q4, R14.Pin_1
  N29: U2.Q5, R15.Pin_1
  N30: U2.Q6, R16.Pin_1
  N31: U2.Q7, R9.Pin_1
  N32: U2.GND, U2.OE
  N33: U2.MR, U2.VCC
  N34: U2.Q0, R11.Pin_1
  N35: R9.Pin_0, LED4.7
  N36: R10.Pin_0, LED4.1
  N37: R11.Pin_0, LED4.11
  N38: R12.Pin_0, LED4.3
  N39: R13.Pin_0, LED4.2
  N40: R14.Pin_0, LED4.4
  N41: R15.Pin_0, LED4.5
  N42: R16.Pin_0, LED4.10
